// Logisim project 1.circ as structural Verilog: 1 circuit, main circuit main
module main (
  input  x_1,
  input  x_2,
  input  x_3,
  output f_1
);

  wire nand_1_out, nand_2_out, nand_3_out, nand_4_out, nand_5_out, nand_6_out;

  nand nand_1 (nand_1_out, x_1, x_1);
  nand nand_2 (nand_2_out, x_2, x_2);
  nand nand_3 (nand_3_out, x_3, x_3);
  nand nand_4 (nand_4_out, nand_1_out, x_2);
  nand nand_5 (nand_5_out, x_1, nand_2_out, nand_3_out);
  nand nand_6 (nand_6_out, x_2, x_3);
  nand nand_7 (f_1, nand_4_out, nand_5_out, nand_6_out);
endmodule
